# Fritzing sketch wiring_diagram (saved by Fritzing 0.9.10b)

parts:
  Part1 = Arduino Nano (Rev3.0)
  R1 = TRIMPOT [maximum_resistance=10kΩ knob_status=50% power=0.5W package=3362u-2]
  R2 = TRIMPOT [maximum_resistance=10kΩ knob_status=50% power=0.5W package=3362u-2]
  LED1 = smd LED [color="Orange (620nm)" package="0805 [SMD]"]
  R3 = Resistor [tolerance=±5% resistance=220 package="0805 [SMD]"]
  Part2 = Adafruit MAX4466 Electret Microphone Amplifier [part_number="Adafruit #1063"]
  J1 = Piezo Speaker

nets:
  GND: Part1.GND, R1.CCW, R2.CCW, LED1.cathode, Part2.GND, J1.pin1
  N1: Part1.D4, J1.pin2
  N2: Part1.D5, R3.Pin_1
  N3: Part1.5V, R1.CW, R2.CW
  N4: Part1.A2, R1.WIPER
  N5: Part1.A1, R2.WIPER
  N6: Part1.A0, Part2.OUT
  3V3: Part1.3V3, Part2.VCC

custom parts:
  Adafruit MAX4466 Electret Microphone Amplifier: Add an ear to your project with this well-designed electret microphone amplifier. This fully assembled and tested board comes with a 20-20KHz electret microphone soldered on. For the amplification, we use the Maxim MAX4466, an op-amp specifically designed for this delicate task! The amplifier has excellent power supply noise rejection, so this amplifier sounds really good and isn't nearly as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
